// Logisim project Multiplicador de 3 bits.circ as structural Verilog: 2 circuits, main circuit main
module main (
  input  a2,
  input  a1,
  input  a0,
  input  b2,
  input  b1,
  input  b0,
  output s0,
  output s1,
  output s2,
  output s3,
  output s4,
  output s5
);

  Multiplicador multiplicador_1 (
    .a2(a2), .a1(a1), .a0(a0), .b2(b2), .b1(b1), .b0(b0), .s0(s0), .s1(s1), .s2(s2), .s3(s3), .s4(s4), .s5(s5));
endmodule

module Multiplicador (
  input  a2,
  input  a1,
  input  a0,
  input  b2,
  input  b1,
  input  b0,
  output s0,
  output s1,
  output s2,
  output s3,
  output s4,
  output s5
);

  wire adder_1_cout, adder_2_cout, adder_2_out, adder_3_cout, adder_3_out, adder_4_cout, adder_5_cout,
       and_2_out, and_3_out, and_4_out, and_5_out, and_6_out, and_7_out, and_8_out, and_9_out;

  and and_1 (s0, b0, a0);
  and and_2 (and_2_out, b0, a1);
  and and_3 (and_3_out, b1, a0);
  and and_4 (and_4_out, b0, a2);
  and and_5 (and_5_out, b1, a1);
  and and_6 (and_6_out, b2, a0);
  and and_7 (and_7_out, b1, a2);
  and and_8 (and_8_out, b2, a1);
  and and_9 (and_9_out, b2, a2);
  Adder #(.width(1)) adder_1 (.a(and_2_out), .b(and_3_out), .out(s1), .cin(1'b0), .cout(adder_1_cout));
  Adder #(.width(1)) adder_2 (.a(and_4_out), .b(and_5_out), .out(adder_2_out), .cin(adder_1_cout), .cout(adder_2_cout));
  Adder #(.width(1)) adder_3 (.a(and_7_out), .b(and_8_out), .out(adder_3_out), .cin(adder_2_cout), .cout(adder_3_cout));
  Adder #(.width(1)) adder_4 (.a(adder_2_out), .b(and_6_out), .out(s2), .cin(1'b0), .cout(adder_4_cout));
  Adder #(.width(1)) adder_5 (.a(adder_3_out), .b(1'b0), .out(s3), .cin(adder_4_cout), .cout(adder_5_cout));
  Adder #(.width(1)) adder_6 (.a(adder_3_cout), .b(and_9_out), .out(s4), .cin(adder_5_cout), .cout(s5));
endmodule
